# Fritzing sketch 回路図_ブレッドボード (saved by Fritzing 0.9.3b)
breadboards: 1

parts:
  W1 = ESPr Developer [package="DIP (Dual Inline) [THT]"]
  J1 = Basic Servo
  J2 = Basic Servo
  J3 = Basic Servo
  IC2 = Voltage Regulator [package=78xxl]
  VCC2 = Battery

nets:
  N1: W1.IO14, J3.pulse
  N2: W1.IO12, J2.pulse
  N3: W1.IO13, J1.pulse
  GND: W1.GND#9, J3.gnd, IC2.GND, VCC2.-
  N4: W1.VIN, IC2.OUT
  VCC: J1.vcc, J2.vcc, J3.vcc, IC2.IN, VCC2.+
